// Logisim project cpu.circ as structural Verilog: 1 circuit, main circuit main
module main (
  input  in_1,
  input  in_2,
  input  in_3,
  input  IRQ
);

  wire ALUOE, clock_1_out, clock_2_out, controlled_buffer_1_out, decoder_1_out0, decoder_1_out1,
       decoder_1_out3, decoder_2_out0, decoder_2_out1, decoder_2_out2, decoder_2_out3, InvClock, IRClk,
       MainClock, MCRST, ML, MR, MW, not_1_out, or_1_out, OverlapClock, PCClk, PCLatchClk, PCLatchOE, PCLoad,
       PCOE, RAClk, RBClk, RCClk, RCOE, SPClk, SPINC, SPLD, SPOE;
  wire [1:0] counter_1_q, PC01;
  wire [3:0] ALUOp;
  wire [4:0] mCodeAL_q, SeqCntr_q;
  wire [7:0] controlled_buffer_4_out, controlled_buffer_5_out, controlled_buffer_6_out, rom_1_data,
       rom_2_data, rom_3_data;
  wire [13:0] PC_q;
  wire [15:0] adder_1_out, and_2_out, BUS, or_5_out, PCLatch_q, RA_q, RB_q, RC_q, SP_q, subtractor_1_out,
       xor_1_out;
  wire [15:4] IR_q;

  Decoder #(.select(2)) decoder_1 (
    .out0(decoder_1_out0), .out1(decoder_1_out1), .out3(decoder_1_out3), .sel({in_1, in_2}));  // open: out2, en
  Clock clock_1 (.out(clock_1_out));
  Clock #(.highDuration(5), .lowDuration(5)) clock_2 (.out(clock_2_out));
  Register #(.width(16)) IR (.D(BUS), .Q({IR_q, ALUOp}), .clk(IRClk));  // open: en, clr
  not not_1 (not_1_out, PCLoad);
  or or_1 (or_1_out, PCClk, PCLoad);
  assign controlled_buffer_1_out = decoder_1_out0 ? clock_1_out : 1'bz;  // Controlled_Buffer controlled_buffer_1
  assign controlled_buffer_1_out = decoder_1_out1 ? clock_2_out : 1'bz;  // Controlled_Buffer controlled_buffer_2
  assign controlled_buffer_1_out = decoder_1_out3 ? in_3 : 1'bz;  // Controlled_Buffer controlled_buffer_3
  Counter #(.width(5), .max('h1f)) SeqCntr (
    .Q(SeqCntr_q), .clk(MainClock), .clr(MCRST));  // open: load, D, count, carry
  Counter #(.width(14), .max('h3fff)) PC (
    .load(PCLoad), .D(BUS[15:2]), .count(not_1_out), .Q(PC_q), .clk(or_1_out));  // open: carry, clr
  Decoder #(.select(2)) decoder_2 (
    .out0(decoder_2_out0), .out1(decoder_2_out1), .out2(decoder_2_out2), .out3(decoder_2_out3),
    .sel(counter_1_q));  // open: en
  Counter #(.width(2), .max('h3)) counter_1 (
    .Q(counter_1_q), .clk(controlled_buffer_1_out));  // open: load, D, count, carry, clr
  Register #(.width(5)) mCodeAL (.D(SeqCntr_q), .Q(mCodeAL_q), .clk(InvClock));  // open: en, clr
  assign BUS = PCOE ? {PC_q, PC01} : 16'bz;  // Controlled_Buffer PCBuf
  or or_2 (MainClock, decoder_2_out0, decoder_2_out1);
  or or_3 (OverlapClock, decoder_2_out1, decoder_2_out2);
  or or_4 (InvClock, decoder_2_out2, decoder_2_out3);
  Register #(.width(16)) PCLatch (.D(BUS), .Q(PCLatch_q), .clk(PCLatchClk));  // open: en, clr
  assign BUS = PCLatchOE ? PCLatch_q : 16'bz;  // Controlled_Buffer PCBuf_2
  ROM #(.addrWidth(16)) rom_1 (.addr({IRQ, IR_q[12:4], ALUOp[3], mCodeAL_q}), .data(rom_1_data));  // open: sel
  assign controlled_buffer_4_out = MainClock ? rom_1_data : 8'bz;  // Controlled_Buffer controlled_buffer_4
  Pull_Resistor pull_resistor_1 (.node(controlled_buffer_4_out));
  assign controlled_buffer_5_out = MainClock ? rom_2_data : 8'bz;  // Controlled_Buffer controlled_buffer_5
  ROM #(.addrWidth(16)) rom_2 (.addr({IRQ, IR_q[12:4], ALUOp[3], mCodeAL_q}), .data(rom_2_data));  // open: sel
  Pull_Resistor pull_resistor_2 (.node(controlled_buffer_5_out));
  assign controlled_buffer_6_out = MainClock ? rom_3_data : 8'bz;  // Controlled_Buffer controlled_buffer_6
  ROM #(.addrWidth(16)) rom_3 (.addr({IRQ, IR_q[12:4], ALUOp[3], mCodeAL_q}), .data(rom_3_data));  // open: sel
  Pull_Resistor pull_resistor_3 (.node(controlled_buffer_6_out));
  Counter #(.width(16), .max('hffff)) SP (
    .load(SPLD), .D(BUS), .count(SPINC), .Q(SP_q), .clk(SPClk));  // open: carry, clr
  Decoder #(.select(3)) decoder_3 (
    .out1(PCOE), .out2(PCLatchOE), .out3(MR), .out4(ALUOE), .out5(SPOE), .out6(RCOE),
    .sel(controlled_buffer_4_out[2:0]));  // open: out0, out7, en
  assign BUS = SPOE ? SP_q : 16'bz;  // Controlled_Buffer SPBuff
  assign {MW, ML, RBClk, RAClk, RCClk, PCLatchClk, PCClk, IRClk} = {controlled_buffer_5_out[2:0], controlled_buffer_4_out[7:3]} & {8{OverlapClock}};  // AND_Gate and_1, 8 bits wide
  Register #(.width(16)) RC (.D(BUS), .Q(RC_q), .clk(RCClk));  // open: en, clr
  assign BUS = RCOE ? RC_q : 16'bz;  // Controlled_Buffer RCBuf
  LED led_1 ();  // open: in
  Register #(.width(16)) RA (.D(BUS), .Q(RA_q), .clk(RAClk));  // open: en, clr
  Register #(.width(16)) RB (.D(BUS), .Q(RB_q), .clk(RBClk));  // open: en, clr
  Adder #(.width(16)) adder_1 (.a(RA_q), .b(RB_q), .out(adder_1_out));  // open: cin, cout
  Subtractor #(.width(16)) subtractor_1 (.a(RA_q), .b(RB_q), .out(subtractor_1_out));  // open: bin, bout
  assign and_2_out = RA_q & RB_q;  // AND_Gate and_2, 16 bits wide
  assign or_5_out = RA_q | RB_q;  // OR_Gate or_5, 16 bits wide
  assign xor_1_out = RA_q ^ RB_q;  // XOR_Gate xor_1, 16 bits wide
  Controlled_Buffer #(.width(16)) controlled_buffer_7 (.in(adder_1_out));  // open: out, en
  Controlled_Buffer #(.width(16)) controlled_buffer_8 (.in(subtractor_1_out));  // open: out, en
  Controlled_Buffer #(.width(16)) controlled_buffer_9 (.in(and_2_out));  // open: out, en
  Controlled_Buffer #(.width(16)) controlled_buffer_10 (.in(or_5_out));  // open: out, en
  Controlled_Buffer #(.width(16)) controlled_buffer_11 (.in(xor_1_out));  // open: out, en

  // Notes on the sheet:
  //   contents of rom_1 (hex, n*v repeats v):
  //   0 1 2 3 4 5 6 7 8 9 a b c d e f 10
  //   contents of rom_2 (hex, n*v repeats v):
  //   16*0 2
endmodule
